# Fritzing sketch Wolverine Claws Schematic (saved by Fritzing 0.9.3b)
breadboards: 1

parts:
  resistor = Resistor [tolerance=±5% resistance=10k package=THT]
  CLS6336HV_servo = Basic Servo
  Arduino_Nano = Arduino Nano (Rev3.0)
  battery = DC Power [voltage=7.4V]
  pushbutton = Pushbutton [package=THT]
  SPST_switch = Pushbutton [package=THT]

nets:
  N1: resistor.Pin_0, Arduino_Nano.D6, pushbutton.leg0
  GND: resistor.Pin_1, CLS6336HV_servo.gnd, Arduino_Nano.GND, battery.V-
  VCC: CLS6336HV_servo.vcc, Arduino_Nano.VIN, SPST_switch.leg1
  N2: CLS6336HV_servo.pulse, Arduino_Nano.D3
  N3: Arduino_Nano.5V, pushbutton.leg1
  N4: battery.V+, SPST_switch.leg0
